# Fritzing sketch schematic (saved by Fritzing 0.9.2b)
breadboards: 1

parts:
  Part1 = Photon
  LCD1 = Adafruit Positive RGB 2x16 LCD
  DS1 = DS18B20 1-Wire Temperature Sensor [part_number=DS18B20]  # not connected
  POT1 = Breadboard Trimpot  # not connected
  R1 = Resistor [tolerance=±5% resistance=10k package=THT]  # not connected
  R2 = Resistor [tolerance=±5% resistance=4.7k package=THT]  # not connected
  S1 = Pushbutton [package="[THT]"]  # not connected
  J1 = Piezo Speaker  # not connected

nets:
  N1: Part1.D1, LCD1.no_name_yet#115
  N2: Part1.D2, LCD1.no_name_yet#116
  N3: Part1.D3, LCD1.no_name_yet#117

custom parts:
  Adafruit Positive RGB 2x16 LCD: Adafruit Positive 2x16 LCD Display with RGB Backlight
